// Logisim project graybox_cpu.circ as structural Verilog: 11 circuits, main circuit main
module main (
  input  [9:0] busin,
  input  clkin,
  input  [9:0] memin,
  output [9:0] busout,
  output [9:0] control,
  output [9:0] mem,
  output clk,
  output [9:0] memout,
  output [9:0] addr,
  output write
);

  wire addrconvert_1_ramon, addrconvert_1_romon, clock_1_out, clock_2_out, clock_3_out, clock_4_out,
       clock_5_out, clock_6_out, controlled_buffer_3_out, jump, module_resolver_1_equal, nor_1_out, por_1_out;
  wire [4:0] addrconvert_1_ramaddr, addrconvert_1_romaddr;
  wire [8:8] pull_resistor_1_node;
  wire [9:0] acc, alu_1_debug_a, alu_1_debug_b, controlbox_1_pcout, memcontrol_1_debug_x,
       module_resolver_1_out_6, ram_1_dout, rom_1_data, SHA_q;

  Clock clock_1 (.out(clock_1_out));
  Clock clock_2 (.out(clock_2_out));
  Clock clock_3 (.out(clock_3_out));
  Clock clock_4 (.out(clock_4_out));
  expansion_auxregs expansion_auxregs_1 (
    .clk(clock_5_out), .busin(busout), .ins(control), .busout(busout));  // open: debug_C, debug_D, debug_E
  Clock clock_5 (.out(clock_5_out));
  module_resolver module_resolver_1 (
    .dir(1'b1), .id(3'b000), .operand(4'b0001), .control(control), .equal(module_resolver_1_equal),
    .out_6(module_resolver_1_out_6));
  // Probe on module_resolver_1_out_6
  Register #(.width(10)) SHA (.D(acc), .en(control[0]), .Q(SHA_q), .clk(clock_1_out));  // open: clr
  Register #(.width(10)) u_ACC (.D(busout), .en(control[0]), .Q(acc), .clk(clock_1_out));  // open: clr
  nor nor_1 (nor_1_out, control[0], control[9]);
  ALU alu_1 (
    .busin(busout), .control(control), .clock(clock_2_out), .acc(acc), .busout(busout),
    .debug_A(alu_1_debug_a), .debug_B(alu_1_debug_b), .jump(jump));
  memcontrol memcontrol_1 (
    .memin(mem), .busin(busout), .pc(controlbox_1_pcout), .control(control), .clock(clock_3_out),
    .busout(busout), .address(addr), .write(write), .debug_X(memcontrol_1_debug_x));
  controlbox controlbox_1 (
    .memin(mem), .busin(busout), .jump(jump), .clock(clock_4_out), .control(control),
    .pcout(controlbox_1_pcout));
  // Probe on SHA_q
  assign busout = module_resolver_1_equal ? SHA_q : 10'bz;  // Controlled_Buffer controlled_buffer_1
  digit_display ACCd (.in_1(acc));
  // Probe on acc
  assign busout = nor_1_out ? acc : 10'bz;  // Controlled_Buffer controlled_buffer_2
  digit_display A (.in_1(alu_1_debug_a));
  // Probe on alu_1_debug_a
  digit_display B (.in_1(alu_1_debug_b));
  // Probe on alu_1_debug_b
  digit_display X (.in_1(memcontrol_1_debug_x));
  // Probe on memcontrol_1_debug_x
  digit_display PC (.in_1(controlbox_1_pcout));
  // Probe on controlbox_1_pcout
  POR #(.PorHighDuration(1), .porTransition(2), .porsize(2)) por_1 (.out(por_1_out));
  Clock clock_6 (.out(clock_6_out));
  ROM #(.addrWidth(5), .dataWidth(10)) rom_1 (.addr(addrconvert_1_romaddr), .data(rom_1_data));
  RAM #(.addrWidth(5), .asyncread("true"), .dataWidth(10)) ram_1 (
    .addr(addrconvert_1_ramaddr), .we(controlled_buffer_3_out), .oe(por_1_out), .clk(clock_6_out),
    .din(busout), .dout(ram_1_dout));
  assign controlled_buffer_3_out = addrconvert_1_ramon ? write : 1'bz;  // Controlled_Buffer controlled_buffer_3
  Pull_Resistor pull_resistor_1 (.node(pull_resistor_1_node[8]));
  Clock clock_7 (.out(clk));
  // Probe on {1'b0, pull_resistor_1_node[8], {8{1'b0}}}
  // Probe on {1'b0, pull_resistor_1_node[8], {8{1'b0}}}
  addrconvert addrconvert_1 (
    .addr(addr), .romaddr(addrconvert_1_romaddr), .romon(addrconvert_1_romon),
    .ramaddr(addrconvert_1_ramaddr), .ramon(addrconvert_1_ramon));
  assign mem = addrconvert_1_romon ? rom_1_data : 10'bz;  // Controlled_Buffer controlled_buffer_4
  assign mem = addrconvert_1_ramon ? ram_1_dout : 10'bz;  // Controlled_Buffer controlled_buffer_5

  assign memout = busout;

  // Other names for the same wires on the sheet: address[9:0] = addr; main_bus[9:0] = busout; mem_write = write

  // Notes on the sheet:
  //   register expansion
  //   logisim bug
  //   imm
  //   submod
  //   operand
  //   dir
  //   contents of rom_1 (hex, n*v repeats v):
  //   250 1 252 1 224 64 41 22 53 50 3 52 26 25e 6
  //   shared lines
endmodule

module controlbox (
  input  [9:0] memin,
  input  [9:0] busin,
  input  jump,
  input  clock,
  output [9:0] control,
  output [9:0] pcout
);

  wire comparator_1_eq, or_1_out;
  wire [9:0] multiplexer_1_out, super_instructions_1_next_ins;

  or or_1 (or_1_out, control[9], comparator_1_eq);
  Counter #(.max('h3ff), .width(10)) PC (
    .load(jump), .D(busin), .count(or_1_out), .Q(pcout), .clk(clock));  // open: carry, up, clr
  super_instructions super_instructions_1 (.instruction(control), .next_ins(super_instructions_1_next_ins));
  Multiplexer #(.width(10)) multiplexer_1 (
    .in0(super_instructions_1_next_ins), .in1(memin), .out(multiplexer_1_out), .sel(comparator_1_eq));
  Comparator #(.mode("unsigned"), .width(10)) comparator_1 (
    .a(control), .b({10{1'b0}}), .eq(comparator_1_eq));  // open: gt, lt
  Register #(.width(10)) INS (.D(multiplexer_1_out), .Q(control), .clk(clock));  // open: en, clr
endmodule

module addrconvert (
  input  [9:0] addr,
  output [4:0] romaddr,
  output romon,
  output [4:0] ramaddr,
  output ramon
);

  wire [9:0] subtractor_1_out;

  Subtractor #(.width(10)) subtractor_1 (.a(addr), .b(10'h64), .out(subtractor_1_out), .bout(romon));  // open: bin
  assign romaddr = romon ? addr[4:0] : 5'bz;  // Controlled_Buffer controlled_buffer_1
  assign ramaddr = ramon ? subtractor_1_out[4:0] : 5'bz;  // Controlled_Buffer controlled_buffer_2
  not not_1 (ramon, romon);

  // Notes on the sheet:
  //   not needed in TT due to game-specific RAM/ROM implementation
endmodule

module memcontrol (
  input  [9:0] memin,
  input  [9:0] busin,
  input  [9:0] pc,
  input  [9:0] control,
  input  clock,
  output [9:0] busout,
  output [9:0] address,
  output write,
  output [9:0] debug_X
);

  wire module_resolver_1_equal, module_resolver_3_equal, module_resolver_4_equal, module_resolver_5_equal,
       or_1_out, or_2_out;
  wire [9:0] module_resolver_1_out_6, module_resolver_2_out_6, module_resolver_3_out_6,
       module_resolver_4_out_6, module_resolver_5_out_6;

  module_resolver module_resolver_1 (
    .dir(1'b1), .id(3'b001), .operand(4'b0000), .control(control), .equal(module_resolver_1_equal),
    .out_6(module_resolver_1_out_6));
  // Probe on module_resolver_1_out_6
  module_resolver module_resolver_2 (
    .id(3'b001), .operand(4'b0001), .control(control), .equal(write), .out_6(module_resolver_2_out_6));  // open: dir
  // Probe on module_resolver_2_out_6
  module_resolver module_resolver_3 (
    .id(3'b001), .operand(4'b0010), .control(control), .equal(module_resolver_3_equal),
    .out_6(module_resolver_3_out_6));  // open: dir
  // Probe on module_resolver_3_out_6
  module_resolver module_resolver_4 (
    .id(3'b001), .operand(4'b0011), .control(control), .equal(module_resolver_4_equal),
    .out_6(module_resolver_4_out_6));  // open: dir
  // Probe on module_resolver_4_out_6
  module_resolver module_resolver_5 (
    .id(3'b000), .operand(4'b0000), .control(control), .equal(module_resolver_5_equal),
    .out_6(module_resolver_5_out_6));  // open: dir
  // Probe on module_resolver_5_out_6
  assign busout = or_1_out ? memin : 10'bz;  // Controlled_Buffer controlled_buffer_1
  or or_1 (or_1_out, module_resolver_1_equal, control[9]);
  Counter #(.max('h3ff), .width(10)) X (
    .load(module_resolver_3_equal), .D(busin), .count(module_resolver_4_equal), .Q(debug_X), .clk(clock));  // open: carry, up, clr
  Multiplexer #(.width(10)) multiplexer_1 (.in0(debug_X), .in1(pc), .out(address), .sel(or_2_out));
  or or_2 (or_2_out, control[9], module_resolver_5_equal);
endmodule

module module_resolver (
  input  [9:0] control,
  input  [2:0] id,
  input  [3:0] operand,
  input  dir,
  output equal,
  output [9:0] out_6
);

  Pull_Resistor pull_resistor_1 (.node(dir));
  Comparator comparator_1 (.a(control[7:0]), .b({id, operand, dir}), .eq(equal));  // open: gt, lt

  assign out_6 = {2'b00, id, operand, dir};

  // Notes on the sheet:
  //   replace with a single equal block
endmodule

module ALU (
  input  [9:0] busin,
  input  [9:0] control,
  input  clock,
  input  [9:0] acc,
  output [9:0] busout,
  output [9:0] debug_A,
  output [9:0] debug_B,
  output jump
);

  wire comparator_1_gt, comparator_2_eq, comparator_2_gt, comparator_2_lt, module_resolver_1_equal,
       module_resolver_2_equal, module_resolver_3_equal, module_resolver_4_equal, module_resolver_5_equal,
       module_resolver_6_equal, module_resolver_7_equal, module_resolver_8_equal, module_resolver_9_equal,
       module_resolver_10_equal, module_resolver_11_equal, module_resolver_12_equal,
       module_resolver_13_equal, module_resolver_14_equal, module_resolver_15_equal,
       module_resolver_16_equal, not_1_out, t_ff_1_q;
  wire [9:0] adder_1_out, divider_1_out, module_resolver_1_out_6, module_resolver_2_out_6,
       module_resolver_3_out_6, module_resolver_4_out_6, module_resolver_5_out_6, module_resolver_6_out_6,
       module_resolver_7_out_6, module_resolver_8_out_6, module_resolver_9_out_6, module_resolver_10_out_6,
       module_resolver_11_out_6, module_resolver_12_out_6, module_resolver_13_out_6,
       module_resolver_14_out_6, module_resolver_15_out_6, module_resolver_16_out_6, multiplexer_1_out,
       multiplier_1_out, subtractor_1_out, subtractor_2_out;

  module_resolver module_resolver_1 (
    .dir(1'b0), .id(3'b010), .operand(4'b1000), .control(control), .equal(module_resolver_1_equal),
    .out_6(module_resolver_1_out_6));
  // Probe on module_resolver_1_out_6
  module_resolver module_resolver_2 (
    .dir(1'b0), .id(3'b010), .operand(4'b1001), .control(control), .equal(module_resolver_2_equal),
    .out_6(module_resolver_2_out_6));
  // Probe on module_resolver_2_out_6
  module_resolver module_resolver_3 (
    .dir(1'b0), .id(3'b010), .operand(4'b0111), .control(control), .equal(module_resolver_3_equal),
    .out_6(module_resolver_3_out_6));
  // Probe on module_resolver_3_out_6
  T_Flip_Flop t_ff_1 (
    .clk(module_resolver_3_equal), .T(module_resolver_3_equal), .Q(t_ff_1_q));  // open: Qn, preset, reset
  Register #(.width(10)) A (.D(busin), .en(module_resolver_1_equal), .Q(debug_A), .clk(clock));  // open: clr
  Register #(.width(10)) B (.D(busin), .en(module_resolver_2_equal), .Q(debug_B), .clk(clock));  // open: clr
  Multiplexer #(.width(10)) multiplexer_1 (.in0(debug_A), .in1(acc), .out(multiplexer_1_out), .sel(t_ff_1_q));
  Adder #(.width(10)) adder_1 (.a(multiplexer_1_out), .b(debug_B), .out(adder_1_out));  // open: cin, cout
  Subtractor #(.width(10)) subtractor_1 (
    .a(multiplexer_1_out), .b(debug_B), .out(subtractor_1_out));  // open: bin, bout
  Multiplier #(.width(10)) multiplier_1 (
    .a(multiplexer_1_out), .b(debug_B), .out(multiplier_1_out));  // open: cin, cout
  Divider #(.width(10)) divider_1 (.a(multiplexer_1_out), .b(debug_B), .out(divider_1_out));  // open: upper, rem
  Subtractor #(.width(10)) subtractor_2 (
    .a(debug_B), .b(multiplexer_1_out), .out(subtractor_2_out));  // open: bin, bout
  assign jump = module_resolver_4_equal ? comparator_1_gt : 1'bz;  // Controlled_Buffer controlled_buffer_1
  Comparator #(.width(10)) comparator_1 (.a(subtractor_2_out), .b({10{1'b0}}), .gt(comparator_1_gt));  // open: eq, lt
  Comparator #(.width(10)) comparator_2 (
    .a(debug_A), .b(debug_B), .gt(comparator_2_gt), .eq(comparator_2_eq), .lt(comparator_2_lt));
  module_resolver module_resolver_4 (
    .id(3'b010), .operand(4'b1010), .control(control), .equal(module_resolver_4_equal),
    .out_6(module_resolver_4_out_6));  // open: dir
  // Probe on module_resolver_4_out_6
  module_resolver module_resolver_5 (
    .id(3'b010), .operand(4'b1011), .control(control), .equal(module_resolver_5_equal),
    .out_6(module_resolver_5_out_6));  // open: dir
  // Probe on module_resolver_5_out_6
  module_resolver module_resolver_6 (
    .id(3'b010), .operand(4'b1100), .control(control), .equal(module_resolver_6_equal),
    .out_6(module_resolver_6_out_6));  // open: dir
  // Probe on module_resolver_6_out_6
  module_resolver module_resolver_7 (
    .id(3'b010), .operand(4'b1101), .control(control), .equal(module_resolver_7_equal),
    .out_6(module_resolver_7_out_6));  // open: dir
  // Probe on module_resolver_7_out_6
  module_resolver module_resolver_8 (
    .id(3'b010), .operand(4'b1110), .control(control), .equal(module_resolver_8_equal),
    .out_6(module_resolver_8_out_6));  // open: dir
  // Probe on module_resolver_8_out_6
  module_resolver module_resolver_9 (
    .id(3'b010), .operand(4'b1111), .control(control), .equal(module_resolver_9_equal),
    .out_6(module_resolver_9_out_6));  // open: dir
  // Probe on module_resolver_9_out_6
  module_resolver module_resolver_10 (
    .dir(1'b1), .id(3'b010), .operand(4'b1000), .control(control), .equal(module_resolver_10_equal),
    .out_6(module_resolver_10_out_6));
  // Probe on module_resolver_10_out_6
  module_resolver module_resolver_11 (
    .dir(1'b1), .id(3'b010), .operand(4'b1001), .control(control), .equal(module_resolver_11_equal),
    .out_6(module_resolver_11_out_6));
  // Probe on module_resolver_11_out_6
  assign busout = module_resolver_12_equal ? adder_1_out : 10'bz;  // Controlled_Buffer controlled_buffer_2
  assign busout = module_resolver_13_equal ? subtractor_1_out : 10'bz;  // Controlled_Buffer controlled_buffer_3
  assign busout = module_resolver_14_equal ? multiplier_1_out : 10'bz;  // Controlled_Buffer controlled_buffer_4
  assign jump = module_resolver_7_equal ? comparator_2_gt : 1'bz;  // Controlled_Buffer controlled_buffer_5
  assign jump = module_resolver_5_equal ? comparator_2_eq : 1'bz;  // Controlled_Buffer controlled_buffer_6
  not not_1 (not_1_out, comparator_2_eq);
  assign jump = module_resolver_6_equal ? not_1_out : 1'bz;  // Controlled_Buffer controlled_buffer_7
  assign jump = module_resolver_8_equal ? comparator_2_lt : 1'bz;  // Controlled_Buffer controlled_buffer_8
  assign busout = module_resolver_10_equal ? debug_A : 10'bz;  // Controlled_Buffer controlled_buffer_9
  assign busout = module_resolver_11_equal ? debug_B : 10'bz;  // Controlled_Buffer controlled_buffer_10
  assign busout = module_resolver_15_equal ? divider_1_out : 10'bz;  // Controlled_Buffer controlled_buffer_11
  assign busout = module_resolver_16_equal ? subtractor_2_out : 10'bz;  // Controlled_Buffer controlled_buffer_12
  assign jump = module_resolver_9_equal ? 1'b1 : 1'bz;  // Controlled_Buffer controlled_buffer_13
  module_resolver module_resolver_12 (
    .dir(1'b1), .id(3'b010), .operand(4'b0000), .control(control), .equal(module_resolver_12_equal),
    .out_6(module_resolver_12_out_6));
  // Probe on module_resolver_12_out_6
  module_resolver module_resolver_13 (
    .dir(1'b1), .id(3'b010), .operand(4'b0001), .control(control), .equal(module_resolver_13_equal),
    .out_6(module_resolver_13_out_6));
  // Probe on module_resolver_13_out_6
  module_resolver module_resolver_14 (
    .dir(1'b1), .id(3'b010), .operand(4'b0010), .control(control), .equal(module_resolver_14_equal),
    .out_6(module_resolver_14_out_6));
  // Probe on module_resolver_14_out_6
  module_resolver module_resolver_15 (
    .dir(1'b1), .id(3'b010), .operand(4'b0011), .control(control), .equal(module_resolver_15_equal),
    .out_6(module_resolver_15_out_6));
  // Probe on module_resolver_15_out_6
  module_resolver module_resolver_16 (
    .dir(1'b1), .id(3'b010), .operand(4'b0100), .control(control), .equal(module_resolver_16_equal),
    .out_6(module_resolver_16_out_6));
  // Probe on module_resolver_16_out_6
endmodule

module super_instructions (
  input  [9:0] instruction,
  output [9:0] next_ins
);

  wire comparator_1_eq, comparator_2_eq, comparator_3_eq, comparator_4_eq, comparator_5_eq;

  Comparator #(.width(10)) comparator_1 (.a(10'h324), .b(instruction), .eq(comparator_1_eq));  // open: gt, lt
  assign next_ins = comparator_1_eq ? 10'h22 : 10'bz;  // Controlled_Buffer controlled_buffer_1
  Comparator #(.width(10)) comparator_2 (.a(10'h350), .b(instruction), .eq(comparator_2_eq));  // open: gt, lt
  assign next_ins = comparator_2_eq ? 10'h352 : 10'bz;  // Controlled_Buffer controlled_buffer_2
  Comparator #(.width(10)) comparator_3 (.a(10'h352), .b(instruction), .eq(comparator_3_eq));  // open: gt, lt
  assign next_ins = comparator_3_eq ? 10'h141 : 10'bz;  // Controlled_Buffer controlled_buffer_3
  Comparator #(.width(10)) comparator_4 (.a(10'h141), .b(instruction), .eq(comparator_4_eq));  // open: gt, lt
  assign next_ins = comparator_4_eq ? 10'h22 : 10'bz;  // Controlled_Buffer controlled_buffer_4
  Comparator #(.width(10)) comparator_5 (.a(10'h121), .b(instruction), .eq(comparator_5_eq));  // open: gt, lt
  assign next_ins = comparator_5_eq ? 10'h50 : 10'bz;  // Controlled_Buffer controlled_buffer_5
  Pull_Resistor pull_resistor_1 (.node(next_ins));

  // Notes on the sheet:
  //   subject to change
endmodule

module digit_display (
  input  [9:0] in_1
);

  wire comparator_1_gt;
  wire [3:0] binary_to_bcd_converter_1_p2, binary_to_bcd_converter_1_p3, binary_to_bcd_converter_1_p4;
  wire [9:0] multiplexer_1_out;

  Multiplexer #(.width(10)) multiplexer_1 (.in0(in_1), .in1(10'h3e7), .out(multiplexer_1_out), .sel(comparator_1_gt));
  Comparator #(.mode("unsigned"), .width(10)) comparator_1 (
    .a(in_1), .b(10'h3e7), .gt(comparator_1_gt));  // open: eq, lt
  // Binary_to_BCD_converter #(.binvalue(10)) binary_to_bcd_converter_1: pin names not known; wires that end beside it: multiplexer_1_out, binary_to_bcd_converter_1_p2, binary_to_bcd_converter_1_p3, binary_to_bcd_converter_1_p4
  Hex_Digit_Display hunds (.value(binary_to_bcd_converter_1_p2));  // open: dp
  Hex_Digit_Display tens (.value(binary_to_bcd_converter_1_p3));  // open: dp
  Hex_Digit_Display ones (.value(binary_to_bcd_converter_1_p4));  // open: dp
endmodule

module external (
);

  wire main_1_clk;
  wire [9:0] expansion_stack_1_busout, main_1_busout, main_1_control;

  expansion_stack expansion_stack_1 (
    .busin(main_1_busout), .ins(main_1_control), .clk(main_1_clk), .busout(expansion_stack_1_busout));
  expansion_auxregs expansion_auxregs_1 (
    .clk(main_1_clk), .busin(main_1_busout), .ins(main_1_control), .busout(expansion_stack_1_busout));  // open: debug_C, debug_D, debug_E
  main main_1 (
    .busin(expansion_stack_1_busout), .control(main_1_control), .clk(main_1_clk), .busout(main_1_busout));  // open: clkin, memin, mem, memout, addr, write

  // Notes on the sheet:
  //   :P disregard that for now
endmodule

module expansion_auxregs (
  input  [9:0] busin,
  input  [9:0] ins,
  input  clk,
  output [9:0] busout,
  output [9:0] debug_C,
  output [9:0] debug_D,
  output [9:0] debug_E
);

  wire module_resolver_1_equal, module_resolver_2_equal, module_resolver_3_equal, module_resolver_4_equal,
       module_resolver_5_equal, module_resolver_6_equal;
  wire [9:0] module_resolver_1_out_6, module_resolver_2_out_6, module_resolver_3_out_6,
       module_resolver_4_out_6, module_resolver_5_out_6, module_resolver_6_out_6;

  module_resolver module_resolver_1 (
    .dir(1'b1), .id(3'b100), .operand(4'b0000), .control(ins), .equal(module_resolver_1_equal),
    .out_6(module_resolver_1_out_6));
  // Probe on module_resolver_1_out_6
  module_resolver module_resolver_2 (
    .dir(1'b1), .id(3'b100), .operand(4'b0001), .control(ins), .equal(module_resolver_2_equal),
    .out_6(module_resolver_2_out_6));
  // Probe on module_resolver_2_out_6
  module_resolver module_resolver_3 (
    .dir(1'b1), .id(3'b100), .operand(4'b0010), .control(ins), .equal(module_resolver_3_equal),
    .out_6(module_resolver_3_out_6));
  // Probe on module_resolver_3_out_6
  module_resolver module_resolver_4 (
    .id(3'b100), .operand(4'b0000), .control(ins), .equal(module_resolver_4_equal),
    .out_6(module_resolver_4_out_6));  // open: dir
  // Probe on module_resolver_4_out_6
  module_resolver module_resolver_5 (
    .id(3'b100), .operand(4'b0001), .control(ins), .equal(module_resolver_5_equal),
    .out_6(module_resolver_5_out_6));  // open: dir
  // Probe on module_resolver_5_out_6
  module_resolver module_resolver_6 (
    .id(3'b100), .operand(4'b0010), .control(ins), .equal(module_resolver_6_equal),
    .out_6(module_resolver_6_out_6));  // open: dir
  // Probe on module_resolver_6_out_6
  assign busout = module_resolver_1_equal ? debug_C : 10'bz;  // Controlled_Buffer controlled_buffer_1
  Register #(.width(10)) C (.D(busin), .en(module_resolver_4_equal), .Q(debug_C), .clk(clk));  // open: clr
  Register #(.width(10)) D (.D(busin), .en(module_resolver_5_equal), .Q(debug_D), .clk(clk));  // open: clr
  assign busout = module_resolver_2_equal ? debug_D : 10'bz;  // Controlled_Buffer controlled_buffer_2
  Register #(.width(10)) E (.D(busin), .en(module_resolver_6_equal), .Q(debug_E), .clk(clk));  // open: clr
  assign busout = module_resolver_3_equal ? debug_E : 10'bz;  // Controlled_Buffer controlled_buffer_3
  digit_display Cd (.in_1(debug_C));
  digit_display Dd (.in_1(debug_D));
  digit_display Ed (.in_1(debug_E));
endmodule

module expansion_stack (
  input  [9:0] busin,
  input  [9:0] ins,
  input  clk,
  output [9:0] busout
);

  wire comparator_1_eq, comparator_2_eq, comparator_3_eq, comparator_4_eq, comparator_5_eq, comparator_6_eq,
       comparator_7_eq, comparator_8_eq, controlled_buffer_1_out, controlled_buffer_2_out,
       controlled_buffer_3_out, controlled_buffer_4_out, controlled_buffer_5_out, controlled_buffer_6_out,
       controlled_buffer_7_out, controlled_buffer_8_out, undriven;
  wire [2:0] STK_q;
  wire [9:0] controlled_buffer_9_out, stack0_q, stack1_q, stack2_q, stack3_q, stack4_q, stack5_q, stack6_q,
       stack7_q;
  wire [9:3] pull_resistor_1_node;

  Counter #(.max('h7), .width(3)) STK (.Q(STK_q), .clk(clk));  // open: load, D, count, carry, up, clr
  Pull_Resistor pull_resistor_1 (.node({pull_resistor_1_node, STK_q}));
  digit_display digit_display_1 (.in_1({pull_resistor_1_node, STK_q}));
  assign controlled_buffer_1_out = comparator_1_eq ? undriven : 1'bz;  // Controlled_Buffer controlled_buffer_1
  Comparator #(.mode("unsigned"), .width(3)) comparator_1 (
    .a(STK_q), .b(3'b000), .eq(comparator_1_eq));  // open: gt, lt
  assign controlled_buffer_2_out = comparator_2_eq ? undriven : 1'bz;  // Controlled_Buffer controlled_buffer_2
  Comparator #(.mode("unsigned"), .width(3)) comparator_2 (
    .a(STK_q), .b(3'b001), .eq(comparator_2_eq));  // open: gt, lt
  assign controlled_buffer_3_out = comparator_3_eq ? undriven : 1'bz;  // Controlled_Buffer controlled_buffer_3
  Comparator #(.mode("unsigned"), .width(3)) comparator_3 (
    .a(STK_q), .b(3'b010), .eq(comparator_3_eq));  // open: gt, lt
  assign controlled_buffer_4_out = comparator_4_eq ? undriven : 1'bz;  // Controlled_Buffer controlled_buffer_4
  Comparator #(.mode("unsigned"), .width(3)) comparator_4 (
    .a(STK_q), .b(3'b011), .eq(comparator_4_eq));  // open: gt, lt
  assign controlled_buffer_5_out = comparator_5_eq ? undriven : 1'bz;  // Controlled_Buffer controlled_buffer_5
  Comparator #(.mode("unsigned"), .width(3)) comparator_5 (
    .a(STK_q), .b(3'b100), .eq(comparator_5_eq));  // open: gt, lt
  assign controlled_buffer_6_out = comparator_6_eq ? undriven : 1'bz;  // Controlled_Buffer controlled_buffer_6
  Comparator #(.mode("unsigned"), .width(3)) comparator_6 (
    .a(STK_q), .b(3'b101), .eq(comparator_6_eq));  // open: gt, lt
  assign controlled_buffer_7_out = comparator_7_eq ? undriven : 1'bz;  // Controlled_Buffer controlled_buffer_7
  Comparator #(.mode("unsigned"), .width(3)) comparator_7 (
    .a(STK_q), .b(3'b110), .eq(comparator_7_eq));  // open: gt, lt
  assign controlled_buffer_8_out = comparator_8_eq ? undriven : 1'bz;  // Controlled_Buffer controlled_buffer_8
  Comparator #(.mode("unsigned"), .width(3)) comparator_8 (
    .a(STK_q), .b(3'b111), .eq(comparator_8_eq));  // open: gt, lt
  assign controlled_buffer_9_out = comparator_1_eq ? stack0_q : 10'bz;  // Controlled_Buffer controlled_buffer_9
  Register #(.width(10)) stack0 (.D(busin), .en(controlled_buffer_1_out), .Q(stack0_q));  // open: clk, clr
  assign controlled_buffer_9_out = comparator_2_eq ? stack1_q : 10'bz;  // Controlled_Buffer controlled_buffer_10
  Register #(.width(10)) stack1 (.D(busin), .en(controlled_buffer_2_out), .Q(stack1_q));  // open: clk, clr
  assign controlled_buffer_9_out = comparator_3_eq ? stack2_q : 10'bz;  // Controlled_Buffer controlled_buffer_11
  Register #(.width(10)) stack2 (.D(busin), .en(controlled_buffer_3_out), .Q(stack2_q));  // open: clk, clr
  assign controlled_buffer_9_out = comparator_4_eq ? stack3_q : 10'bz;  // Controlled_Buffer controlled_buffer_12
  Register #(.width(10)) stack3 (.D(busin), .en(controlled_buffer_4_out), .Q(stack3_q));  // open: clk, clr
  assign controlled_buffer_9_out = comparator_5_eq ? stack4_q : 10'bz;  // Controlled_Buffer controlled_buffer_13
  Register #(.width(10)) stack4 (.D(busin), .en(controlled_buffer_5_out), .Q(stack4_q));  // open: clk, clr
  assign controlled_buffer_9_out = comparator_6_eq ? stack5_q : 10'bz;  // Controlled_Buffer controlled_buffer_14
  Register #(.width(10)) stack5 (.D(busin), .en(controlled_buffer_6_out), .Q(stack5_q));  // open: clk, clr
  assign controlled_buffer_9_out = comparator_7_eq ? stack6_q : 10'bz;  // Controlled_Buffer controlled_buffer_15
  Register #(.width(10)) stack6 (.D(busin), .en(controlled_buffer_7_out), .Q(stack6_q));  // open: clk, clr
  assign controlled_buffer_9_out = comparator_8_eq ? stack7_q : 10'bz;  // Controlled_Buffer controlled_buffer_16
  Register #(.width(10)) stack7 (.D(busin), .en(controlled_buffer_8_out), .Q(stack7_q));  // open: clk, clr
  Controlled_Buffer #(.width(10)) controlled_buffer_17 (.in(controlled_buffer_9_out), .out(busout));  // open: en

  // Notes on the sheet:
  //   unfinished :C
endmodule
